# Fritzing sketch schematic (saved by Fritzing 0.9.5d)
breadboards: 1

parts:
  Part1 = Arduino Uno (Rev3)
  S3 = Pushbutton [package="[THT]"]
  S4 = Pushbutton [package="[THT]"]
  R1 = Resistor [tolerance=±5% resistance=220 package=THT]
  R2 = Resistor [tolerance=±5% resistance=220 package=THT]

nets:
  N1: Part1.GND, S3.Pin_3, S3.Pin_4, S4.Pin_3, S4.Pin_4, R1.Pin_1, R2.Pin_1
  N2: Part1.D3_PWM, S4.Pin_1, S4.Pin_2, R1.Pin_0
  N3: Part1.D5_PWM, S3.Pin_1, S3.Pin_2, R2.Pin_0
