# Fritzing sketch schematic (saved by Fritzing 0.9.5d)
breadboards: 2

parts:
  U1 = 74HC595 [package="DIP16 [THT]"]
  S1 = Pushbutton [package="[SMD]"]
  S2 = Pushbutton [package="[SMD]"]
  S3 = Pushbutton [package="[SMD]"]
  S4 = Pushbutton [package="[SMD]"]
  S5 = Pushbutton [package="[SMD]"]
  S6 = Pushbutton [package="[SMD]"]
  Part1 = Arduino Uno (Rev3)
  D1 = Rectifier Diode [part_number=1N4001 package="300 mil [THT]"]
  D2 = Rectifier Diode [part_number=1N4001 package="300 mil [THT]"]
  D3 = Rectifier Diode [part_number=1N4001 package="300 mil [THT]"]
  D4 = Rectifier Diode [part_number=1N4001 package="300 mil [THT]"]
  D5 = Rectifier Diode [part_number=1N4001 package="300 mil [THT]"]
  D7 = Rectifier Diode [part_number=1N4001 package="300 mil [THT]"]
  R1 = Resistor [tolerance=±5% resistance=10k package=THT]

nets:
  N1: U1.Q1, D1.anode
  N2: U1.Q2, D2.anode
  N3: U1.Q3, D3.anode
  N4: U1.Q4, D4.anode
  N5: U1.Q5, D5.anode
  N6: U1.Q6, D7.anode
  GND: U1.GND, Part1.GND, R1.Pin_0
  N7: U1.SH_CP, Part1.D13/SCK
  N8: U1.ST_CP, Part1.D3_PWM
  N9: U1.DS, Part1.D11_PWM/MOSI
  N10: S1.Pin_1, S1.Pin_2, S2.Pin_1, S2.Pin_2, S3.Pin_1, S3.Pin_2, S4.Pin_1, S4.Pin_2, S5.Pin_1, S5.Pin_2, S6.Pin_1, S6.Pin_2, Part1.D4, R1.Pin_1
  N11: S1.Pin_3, S1.Pin_4, D7.cathode
  N12: S2.Pin_3, S2.Pin_4, D5.cathode
  N13: S3.Pin_3, S3.Pin_4, D4.cathode
  N14: S4.Pin_3, S4.Pin_4, D3.cathode
  N15: S5.Pin_3, S5.Pin_4, D2.cathode
  N16: S6.Pin_3, S6.Pin_4, D1.cathode
